# Fritzing sketch aansluiting motors mosfets (saved by Fritzing 0.9.3b)
breadboards: 1

parts:
  Raspberry_Pi_1 = Raspberry Pi 3 [part_number=RPI-3-V1.2]
  JP3 = Header 8 [package=1x08_smd]
  Q1 = MOSFET-NCHANNEL [package=to-92]
  Q2 = MOSFET-NCHANNEL [package=to-92]
  Q3 = MOSFET-NCHANNEL [package=to-92]
  Q4 = MOSFET-NCHANNEL [package=to-92]
  Q5 = MOSFET-NCHANNEL [package=to-92]
  Q6 = MOSFET-NCHANNEL [package=to-92]
  Q7 = MOSFET-NCHANNEL [package=to-92]
  Q8 = MOSFET-NCHANNEL [package=to-92]
  Q9 = MOSFET-NCHANNEL [package=to-92]
  Q10 = MOSFET-NCHANNEL [package=to-92]
  Q11 = MOSFET-NCHANNEL [package=to-92]

nets:
  N1: Raspberry_Pi_1.GPIO2, Q2.S
  N2: Raspberry_Pi_1.GPIO3, Q7.S
  N3: Raspberry_Pi_1.GND, JP3.8, Q6.D, Q7.D, Q8.D, Q9.D, Q10.D
  N4: Raspberry_Pi_1.GIPO17, Q3.S
  N5: Raspberry_Pi_1.GIPO27, Q5.S
  N6: Raspberry_Pi_1.GIPO22, Q8.S
  N7: Raspberry_Pi_1.GIPO25, Q11.S
  N8: Raspberry_Pi_1.GIPO24, Q10.S
  N9: Raspberry_Pi_1.GIPO23, Q4.S
  N10: Raspberry_Pi_1.GIPO18, Q9.S
  N11: Raspberry_Pi_1.GIPO15, Q6.S
  N12: Raspberry_Pi_1.GIPO14, Q1.S
  N13: JP3.1, Q1.D, Q2.D, Q3.D, Q4.D, Q5.D, Q11.D
  N14: JP3.2, Q2.G, Q7.G
  N15: JP3.3, Q1.G, Q6.G
  N16: JP3.4, Q3.G, Q9.G
  N17: JP3.5, Q5.G, Q8.G
  N18: JP3.6, Q4.G, Q10.G
  N19: JP3.7, Q11.G

notes:
  M_LIGHT
  +
  M1
  M2
  M3
  M4
  M5
  -
  Header Robotarm
