# Fritzing sketch aansluiting motors h-bruggen (saved by Fritzing 0.9.3b)
breadboards: 1

parts:
  M1 = DC Motor
  M2 = DC Motor
  M3 = DC Motor
  M4 = DC Motor
  M5 = DC Motor
  IC1 = H-Bridge [package=THT]
  Raspberry_Pi_1 = Raspberry Pi 3 [part_number=RPI-3-V1.2]
  IC2 = H-Bridge [package=THT]
  IC3 = H-Bridge [package=THT]
  VCC1 = 4 x AAA Battery Mount
  LED1 = LEDs [package=led10mm]
  R1 = Resistor [tolerance=±5% resistance=220 package="0402 [SMD]"]

nets:
  N1: M1.pin_1, IC1.2Y
  N2: M1.pin_2, IC1.1Y
  N3: M2.pin_1, IC1.4Y
  N4: M2.pin_2, IC1.3Y
  N5: M3.pin_1, IC2.4Y
  N6: M3.pin_2, IC2.3Y
  N7: M4.pin_1, IC2.2Y
  N8: M4.pin_2, IC2.1Y
  N9: M5.pin_1, IC3.4Y
  N10: M5.pin_2, IC3.3Y
  N11: IC1.1_2EN, IC1.3_4EN, IC1.VCC1, Raspberry_Pi_1.5V, IC2.1_2EN, IC2.3_4EN, IC2.VCC1, IC3.3_4EN, IC3.VCC1
  N12: IC1.1A, Raspberry_Pi_1.GIPO27
  GND1: IC1.GND1, IC1.GND2, IC1.GND3, IC1.GND4, Raspberry_Pi_1.GND, IC2.GND1, IC2.GND2, IC2.GND3, IC2.GND4, IC3.GND1, IC3.GND2, IC3.GND3, IC3.GND4, VCC1.-, R1.Pin_0
  N13: IC1.2A, Raspberry_Pi_1.GIPO22
  N14: IC1.VCC2, IC2.VCC2, IC3.VCC2, VCC1.+
  N15: IC1.3A, Raspberry_Pi_1.GPIO3
  N16: IC1.4A, Raspberry_Pi_1.GPIO2
  N17: Raspberry_Pi_1.GIPO17, IC3.4A
  N18: Raspberry_Pi_1.GIPO25, LED1.A
  N19: Raspberry_Pi_1.GIPO24, IC2.2A
  N20: Raspberry_Pi_1.GIPO23, IC2.1A
  N21: Raspberry_Pi_1.GIPO18, IC3.3A
  N22: Raspberry_Pi_1.GIPO15, IC2.3A
  N23: Raspberry_Pi_1.GIPO14, IC2.4A

notes:
  M1
  M2
  M3
  M4
  M5
  M_LIGHT
  220Ω resistor
  4x D-battery, niet AAA
